# Fritzing sketch gip (saved by Fritzing 0.8.7b)

parts:
  U1 = ESP32-38PinWide [part_number=ESP32-38PinWide]
  M1 = 1 chan 5v relay module
  LED1 = RGB LED (com. anode, rbg) [package="5 mm [THT]"]
  R1 = Resistor [tolerance=±5% resistance=220 package=THT]
  R2 = Resistor [tolerance=±5% resistance=220 package=THT]
  R3 = Resistor [tolerance=±5% resistance=220 package=THT]
  VCC1 = Battery
  A1 = uhppote electric strike door lock

nets:
  N1: U1.GPIO26, R3.Pin_0
  N2: U1.GPIO27, R2.Pin_0
  N3: U1.GPIO14, R1.Pin_0
  N4: U1.GPIO12, M1.pin_3
  N5: U1.GND, M1.pin_2
  N6: U1.VIN, M1.pin_1
  N7: M1.pin_4, A1.pin2
  N8: M1.pin_5, VCC1.+
  N9: LED1.red_cathode, R1.Pin_1
  N10: LED1.blue_cathode, R2.Pin_1
  N11: LED1.green_cathode, R3.Pin_1

custom parts:
  ESP32-38PinWide: Generic 38-Pin ESP32 with wide format (only access to one side of pins on a breadboard) based on Stephen Lilley's HiLetgo ESP-WROOM-32 ESP32 ESP-32S Development Board.
  1 chan 5v relay module: 1 Channel 5V Relay Module Board Shield with Optocoupler Support High and Low Level Trigger for Arduino.
  uhppote electric strike door lock: UHPPOTE electric strike door lock.
